# Fritzing sketch lampe connecté Lab (saved by Fritzing 0.9.3b)
breadboards: 1

parts:
  Composant1 = Arduino Mega 2560 (Rev3)
  Composant2 = GY-VL53L0XV2 Laser Ranger Module
  S1 = Pushbutton [package="[SMD]"]
  U1 = WS2812 RGB LED strip
  J1 = Power Jack [package=power_jack_pth_lock]

nets:
  N1: Composant1.D21/SCL, Composant1.SCL, Composant2.SCL
  N2: Composant1.D20/SDA, Composant1.SDA, Composant2.SDA
  GND: Composant1.GND, Composant2.GND, S1.Pin_3, S1.Pin_4, U1.GND, J1.GND
  N3: Composant1.D12_PWM, U1.DIN
  VCC: Composant1.5V, Composant2.VCC, U1.VCC, J1.GNDBREAK
  N4: Composant1.D2_PWM, S1.Pin_1, S1.Pin_2

custom parts:
  GY-VL53L0XV2 Laser Ranger Module: The GY-VL53L0XV2 is based on the VL53L0X from ST Microelectronics, a time-of-flight ranging system integrated into a compact module.
  WS2812 RGB LED strip: WS2812 strip
